// Logisim project 1Bitsy.circ as structural Verilog: 1 circuit, main circuit main
module main (
  input  Reset,
  input  Data
);

  wire clock_1_out, n74161_1_pin7, n74161_1_pin10, n74161_1_pin11, n74161_1_pin12, n74161_1_pin13,
       n74161_1_pin14, n74161_2_pin7, n74161_2_pin9, n74161_2_pin10, nor_1_out, nor_2_out, nor_3_out,
       not_1_out;
  wire [3:0] n74161_2_pin14;
  wire [7:0] rom_1_data;

  ROM #(.addrWidth(4)) rom_1 (.addr(n74161_2_pin14), .data(rom_1_data));
  not not_1 (not_1_out, Reset);
  Clock clock_1 (.out(clock_1_out));
  _74161 u_74161_1 (
    .pin1(not_1_out), .pin2(clock_1_out), .pin3(rom_1_data[0]), .pin4(rom_1_data[1]), .pin5(rom_1_data[2]),
    .pin6(rom_1_data[3]), .pin7(n74161_1_pin7), .pin14(n74161_1_pin14), .pin13(n74161_1_pin13),
    .pin12(n74161_1_pin12), .pin11(n74161_1_pin11), .pin10(n74161_1_pin10), .pin9(rom_1_data[4]));  // open: pin15
  _74161 u_74161_2 (
    .pin1(not_1_out), .pin2(clock_1_out), .pin3(rom_1_data[0]), .pin4(rom_1_data[1]), .pin5(rom_1_data[2]),
    .pin6(rom_1_data[3]), .pin7(n74161_2_pin7), .pin14(n74161_2_pin14[0]), .pin13(n74161_2_pin14[1]),
    .pin12(n74161_2_pin14[2]), .pin11(n74161_2_pin14[3]), .pin10(n74161_2_pin10), .pin9(n74161_2_pin9));  // open: pin15
  LED Out0 (.in(n74161_1_pin14));
  LED Out1 (.in(n74161_1_pin13));
  LED Out2 (.in(n74161_1_pin12));
  LED Out3 (.in(n74161_1_pin11));
  nor nor_1 (nor_1_out, Data, Data);
  nor nor_2 (nor_2_out, nor_1_out, nor_3_out);
  nor nor_3 (nor_3_out, rom_1_data[6], rom_1_data[6]);
  nor nor_4 (n74161_2_pin9, nor_2_out, rom_1_data[7]);
  // also tied to GND on the sheet: {n74161_1_pin7, n74161_1_pin10}
  // also tied to VCC on the sheet: {n74161_2_pin7, n74161_2_pin10}
endmodule
